# Fritzing sketch ubicomp circuit (saved by Fritzing 0.9.2b)
breadboards: 1

parts:
  IC1 = AD8232 HeartRate Monitor [part_number=SEN-12650 chip_label=IC package="DIP (Dual Inline) [THT]"]
  M1 = MAX30102
  T1 = LM35 Temperature Sensor [package="TO92 [THT]"]
  Eleman1 = Arduino Uno (Rev3)
  Eleman2 = Arduino Uno (Rev3)
  L298N1 = L298N DC motor driver
  VCC1 = Battery block 9V  # not connected
  M2 = DC Motor  # not connected

nets:
  GND: IC1.GND, M1.GND, T1.GND, Eleman1.GND
  3.3V: IC1.3.3v, M1.VIN, Eleman1.3V3
  N1: IC1.OUTPUT, Eleman1.A0
  N2: IC1.LO-, Eleman1.D11_PWM/MOSI
  N3: IC1.LO+, Eleman1.D10_PWM/SS
  N4: M1.SCL, Eleman1.A5/SCL
  N5: M1.SDA, Eleman1.A4/SDA
  N6: M1.INT, Eleman1.D2
  N7: T1.+Vs, Eleman1.5V
  N8: T1.Vout, Eleman1.A1
  N9: Eleman2.D10_PWM/SS, L298N1.ENA
  N10: Eleman2.D11_PWM/MOSI, L298N1.IN1
  N11: Eleman2.D12/MISO, L298N1.IN2
  GND_2: Eleman2.GND, L298N1.GND

custom parts:
  AD8232 HeartRate Monitor: A DIP stand-in part for whatever IC you want. With 10 pins on a 600mil dual inline package (DIP) footprint.
  MAX30102: Oximeter module using the MAX30102 chip. You may wish to read (and check your module) this post on power problems with these modules: https://reedpaper.wordpress.com/2018/08/22/pulse-oximeter-max30100-max30102-how-to-fix-wrong-board/ . As usual, if you want the mounting holes in pcb, you need to drag a hole over the pad in silkscreen to actually drill the hole (by default they are not drilled)
  L298N DC motor driver: 2x DC motor driver with 78M05 positive voltage regulator (7..35 V) L298N: max 46 V, 2 A Set 5 V Enable jumper to enable 5 V regultor (needed for the L298N) and +5 V output at screw terminal or supply external +5 V at screw terminal Set ENA and/or ENB to +5 V to enable motor permanently or supply ENA and/or ENB with PWM signal IN1 and IN2 set rotation directory for motor A (OUT1/OUT2) IN2 and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
